# Fritzing sketch KubkuinoDNO (saved by Fritzing 0.9.3b)
circuit board: 7.48192cm x 5.34936cm
breadboards: 1

parts:
  22pF = Ceramic Capacitor [capacitance=100nF package="100 mil [THT, multilayer]"]
  C2 = Ceramic Capacitor [capacitance=10pF voltage=6.3V package="100 mil [THT, multilayer]"]
  RESET = Pushbutton [package="[THT]"]
  R1 = Resistor [tolerance=±5% resistance=1k package=THT]
  R3 = Resistor [tolerance=±5% resistance=4.7k package=THT]
  R4 = Resistor [tolerance=±5% resistance=4.7k package=THT]
  R5 = Resistor [tolerance=±5% resistance=4.7k package=THT]
  1W_+/O/- = female pin header, 3 pins [form="♀ (female)" part_number=Calibration]
  J5 = female pin header, 14 pins [form="♀ (female)"]
  J6 = female pin header, 14 pins [form="♀ (female)"]
  I2C = female pin header, 4 pins [form="♀ (female)" part_number=I2C_2]
  I2C_2 = female pin header, 4 pins [form="♀ (female)" part_number=I2C_1]
  Piezo+/- = Piezo Speaker
  Button_+/- = female pin header, 2 pins [form="♀ (female)" part_number=Button]
  U2 = Voltage Regulator - 5V [part_number=LM7805 package="TO220 [THT]"]
  D1 = Diode [package=diode-1n4148]
  B/G/R = female pin header, 3 pins [form="♀ (female)" part_number=LED]
  D2 = Rectifier Diode [part_number=1N4001 package="300 mil [THT]"]
  D3 = Rectifier Diode [part_number=1N4001 package="300 mil [THT]"]
  D4 = Rectifier Diode [part_number=1N4001 package="300 mil [THT]"]
  D5 = Rectifier Diode [part_number=1N4001 package="300 mil [THT]"]
  AC = female pin header, 1 pin [form="♀ (female)"]
  AC_2 = female pin header, 1 pin [form="♀ (female)"]
  C3 = Capacitor Polarized [package=cpol-radial-1000uf-25v]
  C4 = Ceramic Capacitor [capacitance=100nF voltage=10V package="200 mil [THT, multilayer]"]
  Key/Rx/Tx/nc/5V/GND = female pin header, 6 pins [form="♀ (female)"]
  -/+/RST/MOSI/MISO/SCK = female pin header, 6 pins [form="♀ (female)"]
  R2 = Resistor [tolerance=±5% resistance=1k package=THT]
  XTAL1 = Crystal [frequency="16 Mhz" package=THT]
  U1 = atmega328 [package=dip]
  S8050 = TRANSISTOR_NPN [part_number=S8050 package=to-92-ammo]

nets:
  N1: 22pF.0, J6.pin9, XTAL1.pin_0, U1.XLAT1
  GND: 22pF.1, C2.1, RESET.Pin_3, RESET.Pin_4, 1W_+/O/-.pin3, J5.pin7, J6.pin8, I2C.pin3, I2C_2.pin3, Piezo+/-.pin1, Button_+/-.pin1, U2.GND, D4.anode, D5.anode, C3.-, C4.0, Key/Rx/Tx/nc/5V/GND.pin1, -/+/RST/MOSI/MISO/SCK.pin6, U1.GND
  N2: C2.0, J6.pin10, XTAL1.pin_1, U1.XLAT2
  N3: RESET.Pin_1, RESET.Pin_2, R1.Pin_0, J6.pin1, -/+/RST/MOSI/MISO/SCK.pin4, U1.RESET
  N4: R1.Pin_1, R3.Pin_0, R4.Pin_0, R5.Pin_1, 1W_+/O/-.pin1, J5.pin9, J6.pin7, I2C.pin4, I2C_2.pin4, U2.output_voltage, D1.A, C4.1, -/+/RST/MOSI/MISO/SCK.pin5, R2.Pin_1, U1.VCC, U1.AVCC, S8050.E
  N5: R3.Pin_1, J5.pin1, I2C.pin2, I2C_2.pin2, U1.A5
  N6: R4.Pin_1, J5.pin2, I2C.pin1, I2C_2.pin1, U1.A4
  N7: R5.Pin_0, 1W_+/O/-.pin2, J6.pin14, U1.D8
  N8: J5.pin3, B/G/R.pin1, U1.A3
  N9: J5.pin4, B/G/R.pin2, U1.A2
  N10: J5.pin5, B/G/R.pin3, U1.A1
  N11: J5.pin6, U1.A0
  N12: J5.pin8, U1.AREF
  N13: J5.pin10, -/+/RST/MOSI/MISO/SCK.pin1, U1.D13
  N14: J5.pin11, -/+/RST/MOSI/MISO/SCK.pin2, U1.D12
  N15: J5.pin12, -/+/RST/MOSI/MISO/SCK.pin3, U1.D11_(PWM)
  N16: J5.pin13, U1.D10_(PWM)
  N17: J5.pin14, U1.D9_(PWM)
  N18: J6.pin2, U1.D0_(RX)
  N19: J6.pin3, U1.D1_(TX)
  N20: J6.pin4, Button_+/-.pin2, R2.Pin_0, U1.D2
  N21: J6.pin5, Piezo+/-.pin2, U1.D3_(PWM)
  N22: J6.pin6, U1.D4, S8050.B
  N23: J6.pin11, Key/Rx/Tx/nc/5V/GND.pin4, U1.D5_(PWM)
  N24: J6.pin12, Key/Rx/Tx/nc/5V/GND.pin5, U1.D6_(PWM)
  N25: J6.pin13, Key/Rx/Tx/nc/5V/GND.pin6, U1.D7
  N26: U2.input_voltage, D1.C, D2.cathode, D3.cathode, C3.+
  N27: D2.anode, D5.cathode, AC_2.pin1
  N28: D3.anode, D4.cathode, AC.pin1
  N29: Key/Rx/Tx/nc/5V/GND.pin3, S8050.C

notes:
  SDA/SCL/GND/VIN
  Bt:Key/Rx/Tx/5V/3V3/GND
