# Fritzing sketch KubkuinoDNO_Serial (saved by Fritzing 0.9.3b)
circuit board: 7.97539cm x 5.3801cm
breadboards: 2

parts:
  22pF = Ceramic Capacitor [capacitance=100nF package="100 mil [THT, multilayer]"]
  C2 = Ceramic Capacitor [capacitance=10pF voltage=6.3V package="100 mil [THT, multilayer]"]
  R3 = Resistor [tolerance=±5% resistance=4.7k package=THT]
  R4 = Resistor [tolerance=±5% resistance=4.7k package=THT]
  1W_+/O/- = female pin header, 3 pins [form="♀ (female)" part_number=Calibration]
  J5 = female pin header, 14 pins [form="♀ (female)"]
  J6 = female pin header, 14 pins [form="♀ (female)"]
  I2C = female pin header, 4 pins [form="♀ (female)" part_number=I2C_2]
  I2C_2 = female pin header, 4 pins [form="♀ (female)" part_number=I2C_1]
  Piezo+/- = Piezo Speaker
  Button_+/- = female pin header, 2 pins [form="♀ (female)" part_number=Button]
  U2 = Voltage Regulator - 5V [part_number=LM7805 package="TO220 [THT]"]
  D1 = Diode [package=diode-1n4148]
  B/G/R = female pin header, 3 pins [form="♀ (female)" part_number=LED]
  D2 = Rectifier Diode [part_number=1N4001 package="300 mil [THT]"]
  D3 = Rectifier Diode [part_number=1N4001 package="300 mil [THT]"]
  D4 = Rectifier Diode [part_number=1N4001 package="300 mil [THT]"]
  D5 = Rectifier Diode [part_number=1N4001 package="300 mil [THT]"]
  AC = female pin header, 1 pin [form="♀ (female)"]
  AC_2 = female pin header, 1 pin [form="♀ (female)"]
  C3 = Capacitor Polarized [package=cpol-radial-1000uf-25v]
  C4 = Ceramic Capacitor [capacitance=100nF voltage=10V package="200 mil [THT, multilayer]"]
  Key/Rx/Tx/nc/5V/GND = female pin header, 6 pins [form="♀ (female)"]
  -/+/RST/MOSI/MISO/SCK = female pin header, 6 pins [form="♀ (female)"]
  XTAL1 = Crystal [frequency="16 Mhz" package=THT]
  U1 = atmega328 [package=dip]
  S8050 = TRANSISTOR_NPN [part_number=S8050 package=to-92-ammo]
  U3 = Mini-USB _B_ connector with 5th pin broken out. [package=usb-minib]
  IC1 = USB UART [package=ssop28db]
  R1 = Resistor [tolerance=±5% resistance=1k package=THT]
  R2 = Resistor [tolerance=±5% resistance=1k package=THT]
  R5 = Resistor [tolerance=±5% resistance=4.7k package=THT]
  R6 = Resistor [tolerance=±5% resistance=560 package=THT]
  R7 = Resistor [tolerance=±5% resistance=560 package=THT]
  LED1 = LED - 5mm [color="Red (633nm)" package="5 mm [THT]"]
  LED2 = LED - 5mm [color="Red (633nm)" package="5 mm [THT]"]

nets:
  N1: 22pF.0, J6.pin9, XTAL1.pin_0, U1.XLAT1
  GND: 22pF.1, C2.1, 1W_+/O/-.pin3, J5.pin7, J6.pin8, I2C.pin3, I2C_2.pin3, Piezo+/-.pin1, Button_+/-.pin1, U2.GND, D4.anode, D5.anode, C3.-, C4.0, Key/Rx/Tx/nc/5V/GND.pin1, -/+/RST/MOSI/MISO/SCK.pin6, U1.GND, U3.GND, IC1.GND7, IC1.GND18, IC1.GND21, IC1.AGND, IC1.TEST
  N2: C2.0, J6.pin10, XTAL1.pin_1, U1.XLAT2
  VCC: R3.Pin_0, R4.Pin_0, 1W_+/O/-.pin1, J5.pin9, J6.pin7, I2C.pin4, I2C_2.pin4, U2.output_voltage, D1.A, C4.1, -/+/RST/MOSI/MISO/SCK.pin5, U1.VCC, U1.AVCC, S8050.E, U3.VBUS, IC1.VCCIO, IC1.VCC, R1.Pin_1, R2.Pin_1, R5.Pin_1, R6.Pin_1, R7.Pin_1
  N3: R3.Pin_1, J5.pin1, I2C.pin2, I2C_2.pin2, U1.A5
  N4: R4.Pin_1, J5.pin2, I2C.pin1, I2C_2.pin1, U1.A4
  N5: 1W_+/O/-.pin2, J6.pin14, U1.D8, R5.Pin_0
  N6: J5.pin3, B/G/R.pin1, U1.A3
  N7: J5.pin4, B/G/R.pin2, U1.A2
  N8: J5.pin5, B/G/R.pin3, U1.A1
  N9: J5.pin6, U1.A0
  N10: J5.pin8, U1.AREF
  N11: J5.pin10, -/+/RST/MOSI/MISO/SCK.pin1, U1.D13
  N12: J5.pin11, -/+/RST/MOSI/MISO/SCK.pin2, U1.D12
  N13: J5.pin12, -/+/RST/MOSI/MISO/SCK.pin3, U1.D11_(PWM)
  N14: J5.pin13, U1.D10_(PWM)
  N15: J5.pin14, U1.D9_(PWM)
  N16: J6.pin1, -/+/RST/MOSI/MISO/SCK.pin4, U1.RESET, IC1.DTR, R1.Pin_0
  N17: J6.pin2, U1.D0_(RX), IC1.TXD
  N18: J6.pin3, U1.D1_(TX), IC1.RXD
  N19: J6.pin4, Button_+/-.pin2, U1.D2, R2.Pin_0
  N20: J6.pin5, Piezo+/-.pin2, U1.D3_(PWM)
  N21: J6.pin6, U1.D4, S8050.B
  N22: J6.pin11, Key/Rx/Tx/nc/5V/GND.pin4, U1.D5_(PWM)
  N23: J6.pin12, Key/Rx/Tx/nc/5V/GND.pin5, U1.D6_(PWM)
  N24: J6.pin13, Key/Rx/Tx/nc/5V/GND.pin6, U1.D7
  N25: U2.input_voltage, D1.C, D2.cathode, D3.cathode, C3.+
  N26: D2.anode, D5.cathode, AC_2.pin1
  N27: D3.anode, D4.cathode, AC.pin1
  N28: Key/Rx/Tx/nc/5V/GND.pin3, S8050.C
  N29: U3.D+, IC1.USBDP
  N30: U3.D-, IC1.USBDM
  N31: IC1.RXLED, LED2.anode
  N32: IC1.TXLED, LED1.anode
  N33: R6.Pin_0, LED1.cathode
  N34: R7.Pin_0, LED2.cathode

notes:
  SDA/SCL/GND/VIN
  Bt:Key/Rx/Tx/5V/3V3/GND
